// Logisim project practica1-a.circ as structural Verilog: 1 circuit, main circuit main
module main (
  input  [23:0] in_1,
  input  Controlador,
  input  [10:0] in_3,
  output [23:0] out_4
);

  wire clock_1_out, not_1_out;

  Clock clock_1 (.out(clock_1_out));
  assign out_4 = Controlador ? in_1 : 24'bz;  // Controlled_Buffer controlled_buffer_1
  not not_1 (not_1_out, Controlador);
  RAM #(.addrWidth(11), .dataWidth(24)) ram_1 (
    .addr(in_3), .data(out_4), .clk(clock_1_out), .ld(not_1_out));  // open: sel, clr

  // Notes on the sheet:
  //   Bus de datos
  //   Bus de direcciones
  //   Reloj
  //   2048 x 24
  //   Carga datos
endmodule
