// Logisim project practica1-b.circ as structural Verilog: 1 circuit, main circuit main
module main (
  input  [23:0] in_1,
  input  Controlador,
  input  [9:0] in_3,
  output [23:0] out_4
);

  wire clock_1_out, not_1_out, not_2_out, not_3_out;

  Clock clock_1 (.out(clock_1_out));
  assign out_4[7:0] = Controlador ? in_1[7:0] : 8'bz;  // Controlled_Buffer controlled_buffer_1
  not not_1 (not_1_out, Controlador);
  assign out_4[15:8] = Controlador ? in_1[15:8] : 8'bz;  // Controlled_Buffer controlled_buffer_2
  not not_2 (not_2_out, Controlador);
  assign out_4[23:16] = Controlador ? in_1[23:16] : 8'bz;  // Controlled_Buffer controlled_buffer_3
  not not_3 (not_3_out, Controlador);
  RAM #(.addrWidth(10)) ram_1 (.addr(in_3), .data(out_4[7:0]), .clk(clock_1_out), .ld(not_1_out));  // open: sel, clr
  RAM #(.addrWidth(10)) ram_2 (.addr(in_3), .data(out_4[15:8]), .clk(clock_1_out), .ld(not_2_out));  // open: sel, clr
  RAM #(.addrWidth(10)) ram_3 (.addr(in_3), .data(out_4[23:16]), .clk(clock_1_out), .ld(not_3_out));  // open: sel, clr

  // Notes on the sheet:
  //   Bus de Datos
  //   Bus de Direcciones
  //   Reloj
  //   Carga de datos
endmodule
