// Logisim project practica1-c.circ as structural Verilog: 1 circuit, main circuit main
module main (
  input  DE5,
  input  DE4,
  input  DE3,
  input  DE2,
  input  DE1,
  input  DE0,
  input  Dir_0,
  input  Dir_1,
  input  Dir_2,
  input  Dir_3,
  input  SEL,
  input  LEC,
  input  SAL,
  output out_14,
  output out_15,
  output out_16,
  output out_17,
  output out_18,
  output out_19
);

  wire and_1_out, and_2_out, and_3_out, and_4_out, and_5_out, and_6_out, and_7_out, and_8_out, and_9_out,
       and_10_out, and_11_out, and_12_out, and_13_out, and_14_out, and_15_out, and_16_out, and_17_out,
       and_18_out, and_19_out, and_20_out, and_21_out, and_22_out, and_23_out, and_24_out, and_25_out,
       and_26_out, and_27_out, and_28_out, and_29_out, and_30_out, and_31_out, and_32_out, and_33_out,
       and_34_out, and_35_out, and_36_out, and_37_out, and_38_out, and_39_out, and_40_out, and_41_out,
       and_42_out, and_43_out, and_44_out, and_45_out, and_46_out, and_47_out, and_48_out, and_49_out,
       and_50_out, and_51_out, and_52_out, and_53_out, and_54_out, and_55_out, and_56_out, and_57_out,
       and_58_out, and_59_out, and_60_out, and_61_out, and_62_out, and_63_out, and_64_out, and_65_out,
       and_66_out, and_67_out, and_68_out, and_69_out, and_70_out, and_71_out, and_72_out, and_73_out,
       and_74_out, d_ff_1_q, d_ff_2_q, d_ff_3_q, d_ff_4_q, d_ff_5_q, d_ff_6_q, d_ff_7_q, d_ff_8_q, d_ff_9_q,
       d_ff_10_q, d_ff_11_q, d_ff_12_q, d_ff_13_q, d_ff_14_q, d_ff_15_q, d_ff_16_q, d_ff_17_q, d_ff_18_q,
       d_ff_19_q, d_ff_20_q, d_ff_21_q, d_ff_22_q, d_ff_23_q, d_ff_24_q, d_ff_25_q, d_ff_26_q, d_ff_27_q,
       d_ff_28_q, d_ff_29_q, d_ff_30_q, d_ff_31_q, d_ff_32_q, d_ff_33_q, d_ff_34_q, d_ff_35_q, d_ff_36_q,
       d_ff_37_q, d_ff_38_q, d_ff_39_q, d_ff_40_q, d_ff_41_q, d_ff_42_q, d_ff_43_q, d_ff_44_q, d_ff_45_q,
       d_ff_46_q, d_ff_47_q, d_ff_48_q, d_ff_49_q, d_ff_50_q, d_ff_51_q, d_ff_52_q, d_ff_53_q, d_ff_54_q,
       not_1_out, not_2_out, not_3_out, not_4_out, not_5_out, not_6_out, not_7_out, not_8_out, not_9_out,
       not_10_out, not_11_out, not_12_out, not_13_out, not_14_out, not_15_out, not_16_out, not_17_out,
       not_18_out, not_19_out, not_20_out, not_21_out, not_22_out, not_23_out, not_24_out, or_1_out,
       or_2_out, or_3_out, or_4_out, or_5_out, or_6_out;

  not not_1 (not_1_out, Dir_0);
  not not_2 (not_2_out, Dir_1);
  not not_3 (not_3_out, Dir_2);
  not not_4 (not_4_out, Dir_3);
  not not_5 (not_5_out, Dir_1);
  not not_6 (not_6_out, Dir_2);
  not not_7 (not_7_out, Dir_3);
  not not_8 (not_8_out, Dir_0);
  not not_9 (not_9_out, Dir_2);
  not not_10 (not_10_out, Dir_3);
  not not_11 (not_11_out, Dir_2);
  not not_12 (not_12_out, Dir_3);
  not not_13 (not_13_out, Dir_0);
  not not_14 (not_14_out, Dir_1);
  not not_15 (not_15_out, Dir_3);
  not not_16 (not_16_out, Dir_1);
  not not_17 (not_17_out, Dir_3);
  not not_18 (not_18_out, Dir_0);
  not not_19 (not_19_out, Dir_3);
  not not_20 (not_20_out, Dir_3);
  not not_21 (not_21_out, Dir_0);
  not not_22 (not_22_out, Dir_1);
  not not_23 (not_23_out, Dir_2);
  and and_1 (and_1_out, not_1_out, not_2_out, not_3_out, not_4_out);
  and and_2 (and_2_out, Dir_0, not_5_out, not_6_out, not_7_out);
  and and_3 (and_3_out, not_8_out, Dir_1, not_9_out, not_10_out);
  and and_4 (and_4_out, Dir_0, Dir_1, not_11_out, not_12_out);
  and and_5 (and_5_out, not_13_out, not_14_out, Dir_2, not_15_out);
  and and_6 (and_6_out, Dir_0, not_16_out, Dir_2, not_17_out);
  and and_7 (and_7_out, not_18_out, Dir_1, Dir_2, not_19_out);
  and and_8 (and_8_out, Dir_0, Dir_1, Dir_2, not_20_out);
  and and_9 (and_9_out, not_21_out, not_22_out, not_23_out, Dir_3);
  and and_10 (and_10_out, SEL, not_24_out);
  not not_24 (not_24_out, LEC);
  and and_11 (and_11_out, and_10_out, and_1_out);
  and and_12 (and_12_out, and_10_out, and_2_out);
  and and_13 (and_13_out, and_10_out, and_3_out);
  and and_14 (and_14_out, and_10_out, and_4_out);
  and and_15 (and_15_out, and_10_out, and_5_out);
  and and_16 (and_16_out, and_10_out, and_6_out);
  and and_17 (and_17_out, and_10_out, and_7_out);
  and and_18 (and_18_out, and_10_out, and_8_out);
  and and_19 (and_19_out, and_10_out, and_9_out);
  and and_20 (and_20_out, LEC, SEL, SAL);
  D_Flip_Flop d_ff_1 (.clk(and_11_out), .D(DE0), .Q(d_ff_1_q));  // open: Qn, preset, en, reset
  D_Flip_Flop d_ff_2 (.clk(and_12_out), .D(DE0), .Q(d_ff_2_q));  // open: Qn, preset, en, reset
  D_Flip_Flop d_ff_3 (.clk(and_13_out), .D(DE0), .Q(d_ff_3_q));  // open: Qn, preset, en, reset
  D_Flip_Flop d_ff_4 (.clk(and_14_out), .D(DE0), .Q(d_ff_4_q));  // open: Qn, preset, en, reset
  D_Flip_Flop d_ff_5 (.clk(and_15_out), .D(DE0), .Q(d_ff_5_q));  // open: Qn, preset, en, reset
  D_Flip_Flop d_ff_6 (.clk(and_16_out), .D(DE0), .Q(d_ff_6_q));  // open: Qn, preset, en, reset
  D_Flip_Flop d_ff_7 (.clk(and_17_out), .D(DE0), .Q(d_ff_7_q));  // open: Qn, preset, en, reset
  D_Flip_Flop d_ff_8 (.clk(and_18_out), .D(DE0), .Q(d_ff_8_q));  // open: Qn, preset, en, reset
  D_Flip_Flop d_ff_9 (.clk(and_19_out), .D(DE0), .Q(d_ff_9_q));  // open: Qn, preset, en, reset
  and and_21 (and_21_out, d_ff_1_q, and_1_out);
  and and_22 (and_22_out, d_ff_2_q, and_2_out);
  and and_23 (and_23_out, d_ff_3_q, and_3_out);
  and and_24 (and_24_out, d_ff_4_q, and_4_out);
  and and_25 (and_25_out, d_ff_5_q, and_5_out);
  and and_26 (and_26_out, d_ff_6_q, and_6_out);
  and and_27 (and_27_out, d_ff_7_q, and_7_out);
  and and_28 (and_28_out, d_ff_8_q, and_8_out);
  or or_1 (or_1_out, and_21_out, and_22_out, and_23_out, and_24_out, and_25_out, and_26_out, and_27_out, and_28_out, and_29_out);
  assign out_19 = and_20_out ? or_1_out : 1'bz;  // Controlled_Buffer controlled_buffer_1
  and and_29 (and_29_out, d_ff_9_q, and_9_out);
  D_Flip_Flop d_ff_10 (.clk(and_11_out), .D(DE1), .Q(d_ff_10_q));  // open: Qn, preset, en, reset
  and and_30 (and_30_out, d_ff_10_q, and_1_out);
  D_Flip_Flop d_ff_11 (.clk(and_12_out), .D(DE1), .Q(d_ff_11_q));  // open: Qn, preset, en, reset
  and and_31 (and_31_out, d_ff_11_q, and_2_out);
  D_Flip_Flop d_ff_12 (.clk(and_13_out), .D(DE1), .Q(d_ff_12_q));  // open: Qn, preset, en, reset
  D_Flip_Flop d_ff_13 (.clk(and_14_out), .D(DE1), .Q(d_ff_13_q));  // open: Qn, preset, en, reset
  D_Flip_Flop d_ff_14 (.clk(and_15_out), .D(DE1), .Q(d_ff_14_q));  // open: Qn, preset, en, reset
  D_Flip_Flop d_ff_15 (.clk(and_16_out), .D(DE1), .Q(d_ff_15_q));  // open: Qn, preset, en, reset
  D_Flip_Flop d_ff_16 (.clk(and_17_out), .D(DE1), .Q(d_ff_16_q));  // open: Qn, preset, en, reset
  D_Flip_Flop d_ff_17 (.clk(and_18_out), .D(DE1), .Q(d_ff_17_q));  // open: Qn, preset, en, reset
  D_Flip_Flop d_ff_18 (.clk(and_19_out), .D(DE1), .Q(d_ff_18_q));  // open: Qn, preset, en, reset
  and and_32 (and_32_out, d_ff_12_q, and_3_out);
  and and_33 (and_33_out, d_ff_13_q, and_4_out);
  and and_34 (and_34_out, d_ff_14_q, and_5_out);
  and and_35 (and_35_out, d_ff_15_q, and_6_out);
  or or_2 (or_2_out, and_30_out, and_31_out, and_32_out, and_33_out, and_34_out, and_35_out, and_36_out, and_37_out, and_38_out);
  and and_36 (and_36_out, d_ff_16_q, and_7_out);
  and and_37 (and_37_out, d_ff_17_q, and_8_out);
  and and_38 (and_38_out, d_ff_18_q, and_9_out);
  assign out_18 = and_20_out ? or_2_out : 1'bz;  // Controlled_Buffer controlled_buffer_2
  D_Flip_Flop d_ff_19 (.clk(and_11_out), .D(DE2), .Q(d_ff_19_q));  // open: Qn, preset, en, reset
  D_Flip_Flop d_ff_20 (.clk(and_12_out), .D(DE2), .Q(d_ff_20_q));  // open: Qn, preset, en, reset
  D_Flip_Flop d_ff_21 (.clk(and_13_out), .D(DE2), .Q(d_ff_21_q));  // open: Qn, preset, en, reset
  D_Flip_Flop d_ff_22 (.clk(and_14_out), .D(DE2), .Q(d_ff_22_q));  // open: Qn, preset, en, reset
  D_Flip_Flop d_ff_23 (.clk(and_15_out), .D(DE2), .Q(d_ff_23_q));  // open: Qn, preset, en, reset
  D_Flip_Flop d_ff_24 (.clk(and_16_out), .D(DE2), .Q(d_ff_24_q));  // open: Qn, preset, en, reset
  D_Flip_Flop d_ff_25 (.clk(and_17_out), .D(DE2), .Q(d_ff_25_q));  // open: Qn, preset, en, reset
  D_Flip_Flop d_ff_26 (.clk(and_18_out), .D(DE2), .Q(d_ff_26_q));  // open: Qn, preset, en, reset
  D_Flip_Flop d_ff_27 (.clk(and_19_out), .D(DE2), .Q(d_ff_27_q));  // open: Qn, preset, en, reset
  and and_39 (and_39_out, d_ff_19_q, and_1_out);
  and and_40 (and_40_out, d_ff_20_q, and_2_out);
  and and_41 (and_41_out, d_ff_21_q, and_3_out);
  and and_42 (and_42_out, d_ff_22_q, and_4_out);
  and and_43 (and_43_out, d_ff_23_q, and_5_out);
  and and_44 (and_44_out, d_ff_24_q, and_6_out);
  and and_45 (and_45_out, d_ff_25_q, and_7_out);
  and and_46 (and_46_out, d_ff_26_q, and_8_out);
  or or_3 (or_3_out, and_39_out, and_40_out, and_41_out, and_42_out, and_43_out, and_44_out, and_45_out, and_46_out, and_47_out);
  assign out_17 = and_20_out ? or_3_out : 1'bz;  // Controlled_Buffer controlled_buffer_3
  and and_47 (and_47_out, d_ff_27_q, and_9_out);
  D_Flip_Flop d_ff_28 (.clk(and_11_out), .D(DE3), .Q(d_ff_28_q));  // open: Qn, preset, en, reset
  and and_48 (and_48_out, d_ff_28_q, and_1_out);
  D_Flip_Flop d_ff_29 (.clk(and_12_out), .D(DE3), .Q(d_ff_29_q));  // open: Qn, preset, en, reset
  and and_49 (and_49_out, d_ff_29_q, and_2_out);
  D_Flip_Flop d_ff_30 (.clk(and_13_out), .D(DE3), .Q(d_ff_30_q));  // open: Qn, preset, en, reset
  D_Flip_Flop d_ff_31 (.clk(and_14_out), .D(DE3), .Q(d_ff_31_q));  // open: Qn, preset, en, reset
  D_Flip_Flop d_ff_32 (.clk(and_15_out), .D(DE3), .Q(d_ff_32_q));  // open: Qn, preset, en, reset
  D_Flip_Flop d_ff_33 (.clk(and_16_out), .D(DE3), .Q(d_ff_33_q));  // open: Qn, preset, en, reset
  D_Flip_Flop d_ff_34 (.clk(and_17_out), .D(DE3), .Q(d_ff_34_q));  // open: Qn, preset, en, reset
  D_Flip_Flop d_ff_35 (.clk(and_18_out), .D(DE3), .Q(d_ff_35_q));  // open: Qn, preset, en, reset
  D_Flip_Flop d_ff_36 (.clk(and_19_out), .D(DE3), .Q(d_ff_36_q));  // open: Qn, preset, en, reset
  and and_50 (and_50_out, d_ff_30_q, and_3_out);
  and and_51 (and_51_out, d_ff_31_q, and_4_out);
  and and_52 (and_52_out, d_ff_32_q, and_5_out);
  and and_53 (and_53_out, d_ff_33_q, and_6_out);
  or or_4 (or_4_out, and_48_out, and_49_out, and_50_out, and_51_out, and_52_out, and_53_out, and_54_out, and_55_out, and_56_out);
  and and_54 (and_54_out, d_ff_34_q, and_7_out);
  and and_55 (and_55_out, d_ff_35_q, and_8_out);
  and and_56 (and_56_out, d_ff_36_q, and_9_out);
  assign out_16 = and_20_out ? or_4_out : 1'bz;  // Controlled_Buffer controlled_buffer_4
  D_Flip_Flop d_ff_37 (.clk(and_11_out), .D(DE4), .Q(d_ff_37_q));  // open: Qn, preset, en, reset
  D_Flip_Flop d_ff_38 (.clk(and_12_out), .D(DE4), .Q(d_ff_38_q));  // open: Qn, preset, en, reset
  D_Flip_Flop d_ff_39 (.clk(and_13_out), .D(DE4), .Q(d_ff_39_q));  // open: Qn, preset, en, reset
  D_Flip_Flop d_ff_40 (.clk(and_14_out), .D(DE4), .Q(d_ff_40_q));  // open: Qn, preset, en, reset
  D_Flip_Flop d_ff_41 (.clk(and_15_out), .D(DE4), .Q(d_ff_41_q));  // open: Qn, preset, en, reset
  D_Flip_Flop d_ff_42 (.clk(and_16_out), .D(DE4), .Q(d_ff_42_q));  // open: Qn, preset, en, reset
  D_Flip_Flop d_ff_43 (.clk(and_17_out), .D(DE4), .Q(d_ff_43_q));  // open: Qn, preset, en, reset
  D_Flip_Flop d_ff_44 (.clk(and_18_out), .D(DE4), .Q(d_ff_44_q));  // open: Qn, preset, en, reset
  D_Flip_Flop d_ff_45 (.clk(and_19_out), .D(DE4), .Q(d_ff_45_q));  // open: Qn, preset, en, reset
  and and_57 (and_57_out, d_ff_37_q, and_1_out);
  and and_58 (and_58_out, d_ff_38_q, and_2_out);
  and and_59 (and_59_out, d_ff_39_q, and_3_out);
  and and_60 (and_60_out, d_ff_40_q, and_4_out);
  and and_61 (and_61_out, d_ff_41_q, and_5_out);
  and and_62 (and_62_out, d_ff_42_q, and_6_out);
  and and_63 (and_63_out, d_ff_43_q, and_7_out);
  or or_5 (or_5_out, and_57_out, and_58_out, and_59_out, and_60_out, and_61_out, and_62_out, and_63_out, and_64_out, and_65_out);
  assign out_15 = and_20_out ? or_5_out : 1'bz;  // Controlled_Buffer controlled_buffer_5
  and and_64 (and_64_out, d_ff_44_q, and_8_out);
  and and_65 (and_65_out, d_ff_45_q, and_9_out);
  D_Flip_Flop d_ff_46 (.clk(and_11_out), .D(DE5), .Q(d_ff_46_q));  // open: Qn, preset, en, reset
  and and_66 (and_66_out, d_ff_46_q, and_1_out);
  D_Flip_Flop d_ff_47 (.clk(and_12_out), .D(DE5), .Q(d_ff_47_q));  // open: Qn, preset, en, reset
  D_Flip_Flop d_ff_48 (.clk(and_13_out), .D(DE5), .Q(d_ff_48_q));  // open: Qn, preset, en, reset
  D_Flip_Flop d_ff_49 (.clk(and_14_out), .D(DE5), .Q(d_ff_49_q));  // open: Qn, preset, en, reset
  D_Flip_Flop d_ff_50 (.clk(and_15_out), .D(DE5), .Q(d_ff_50_q));  // open: Qn, preset, en, reset
  D_Flip_Flop d_ff_51 (.clk(and_16_out), .D(DE5), .Q(d_ff_51_q));  // open: Qn, preset, en, reset
  D_Flip_Flop d_ff_52 (.clk(and_17_out), .D(DE5), .Q(d_ff_52_q));  // open: Qn, preset, en, reset
  D_Flip_Flop d_ff_53 (.clk(and_18_out), .D(DE5), .Q(d_ff_53_q));  // open: Qn, preset, en, reset
  D_Flip_Flop d_ff_54 (.clk(and_19_out), .D(DE5), .Q(d_ff_54_q));  // open: Qn, preset, en, reset
  and and_67 (and_67_out, d_ff_47_q, and_2_out);
  and and_68 (and_68_out, d_ff_48_q, and_3_out);
  and and_69 (and_69_out, d_ff_49_q, and_4_out);
  and and_70 (and_70_out, d_ff_50_q, and_5_out);
  or or_6 (or_6_out, and_66_out, and_67_out, and_68_out, and_69_out, and_70_out, and_71_out, and_72_out, and_73_out, and_74_out);
  and and_71 (and_71_out, d_ff_51_q, and_6_out);
  and and_72 (and_72_out, d_ff_52_q, and_7_out);
  and and_73 (and_73_out, d_ff_53_q, and_8_out);
  and and_74 (and_74_out, d_ff_54_q, and_9_out);
  assign out_14 = and_20_out ? or_6_out : 1'bz;  // Controlled_Buffer controlled_buffer_6
endmodule
