// Logisim project practica2-b.circ as structural Verilog: 1 circuit, main circuit main
module main (
  input  [23:0] in_1,
  input  [15:0] in_2,
  output [23:0] out_3
);

  wire clock_1_out, nand_1_out, not_1_out, not_2_out, not_3_out, not_4_out, not_5_out, not_6_out, not_7_out,
       not_8_out, not_9_out, not_10_out;
  wire [23:0] register_2_q;

  not not_1 (not_1_out, in_2[0]);
  not not_2 (not_2_out, in_2[1]);
  not not_3 (not_3_out, in_2[2]);
  not not_4 (not_4_out, in_2[4]);
  not not_5 (not_5_out, in_2[5]);
  not not_6 (not_6_out, in_2[9]);
  not not_7 (not_7_out, in_2[12]);
  not not_8 (not_8_out, in_2[13]);
  not not_9 (not_9_out, in_2[14]);
  nand nand_1 (nand_1_out, ~not_1_out, ~not_2_out, ~not_3_out, ~in_2[3], ~not_4_out, ~not_5_out, ~in_2[6], ~in_2[7], ~in_2[8], ~not_6_out, ~in_2[10], ~in_2[11], ~not_7_out, ~not_8_out, ~not_9_out, ~in_2[15]);  // NAND_Gate
  not not_10 (not_10_out, nand_1_out);
  Register #(.width(24)) register_1 (.D(register_2_q), .en(not_10_out), .Q(out_3), .clk(clock_1_out));  // open: clr
  Register #(.width(24)) register_2 (.D(in_1), .en(not_10_out), .Q(register_2_q), .clk(clock_1_out));  // open: clr
  Clock clock_1 (.out(clock_1_out));

  // Notes on the sheet:
  //   Bus de Direcciones
  //   Bus de Datos
  //   Controlador de lectura
  //   Controlador
  //   Cargar datos
endmodule
