// Logisim project practica2-c.circ as structural Verilog: 1 circuit, main circuit main
module main (
  input  [3:0] Entrada,
  input  [9:0] in_2,
  output [3:0] Salida
);

  wire _00_out, _01_out, _10_out, _11_out, and_1_out, and_2_out, and_3_out, clock_1_out;
  wire [3:0] controlled_buffer_1_out, controlled_buffer_2_out, controlled_buffer_4_out,
       controlled_buffer_6_out, controlled_buffer_8_out, controlled_buffer_10_out, R0_q, R1_q, R2_q, R3_q;

  and and_1 (and_1_out, in_2[2], ~in_2[4], ~in_2[5], ~in_2[6], ~in_2[7], in_2[8], in_2[9]);  // AND_Gate
  Clock clock_1 (.out(clock_1_out));
  and _00 (_00_out, ~in_2[0], ~in_2[1]);  // AND_Gate
  Register #(.width(4)) R0 (.D(controlled_buffer_2_out), .en(_00_out), .Q(R0_q), .clk(clock_1_out));  // open: clr
  Register #(.width(4)) R1 (.D(controlled_buffer_4_out), .en(_01_out), .Q(R1_q), .clk(clock_1_out));  // open: clr
  and _01 (_01_out, in_2[0], ~in_2[1]);  // AND_Gate
  Register #(.width(4)) R2 (.D(controlled_buffer_6_out), .en(_10_out), .Q(R2_q), .clk(clock_1_out));  // open: clr
  and _10 (_10_out, ~in_2[0], in_2[1]);  // AND_Gate
  and _11 (_11_out, in_2[0], in_2[1]);
  Register #(.width(4)) R3 (.D(controlled_buffer_8_out), .en(_11_out), .Q(R3_q), .clk(clock_1_out));  // open: clr
  assign controlled_buffer_1_out = _00_out ? R0_q : 4'bz;  // Controlled_Buffer controlled_buffer_1
  assign controlled_buffer_2_out = _00_out ? controlled_buffer_10_out : 4'bz;  // Controlled_Buffer controlled_buffer_2
  assign controlled_buffer_1_out = _01_out ? R1_q : 4'bz;  // Controlled_Buffer controlled_buffer_3
  assign controlled_buffer_4_out = _01_out ? controlled_buffer_10_out : 4'bz;  // Controlled_Buffer controlled_buffer_4
  assign controlled_buffer_1_out = _10_out ? R2_q : 4'bz;  // Controlled_Buffer controlled_buffer_5
  assign controlled_buffer_6_out = _10_out ? controlled_buffer_10_out : 4'bz;  // Controlled_Buffer controlled_buffer_6
  assign controlled_buffer_1_out = _11_out ? R3_q : 4'bz;  // Controlled_Buffer controlled_buffer_7
  assign controlled_buffer_8_out = _11_out ? controlled_buffer_10_out : 4'bz;  // Controlled_Buffer controlled_buffer_8
  and and_2 (and_2_out, ~in_2[3], and_1_out);  // AND_Gate
  and and_3 (and_3_out, in_2[3], and_1_out);
  assign Salida = and_2_out ? controlled_buffer_1_out : 4'bz;  // Controlled_Buffer controlled_buffer_9
  assign controlled_buffer_10_out = and_3_out ? Entrada : 4'bz;  // Controlled_Buffer controlled_buffer_10

  // Notes on the sheet:
  //   INSTRUCCIONES DE E/S
  //   Escritura
  //   Lectura
endmodule
