// Logisim project ALU-2.circ as structural Verilog: 1 circuit, main circuit main
// Overflow
module main (
  input  [3:0] Datos,
  input  Set_A,
  input  Set_B,
  input  Set_C,
  input  [2:0] Banderas,
  input  Bandera,
  output [3:0] Salida,
  output Sobrecarga
);

  wire comparator_1_eq, comparator_1_gt, comparator_1_lt, not_3_out, or_2_out, or_3_out, Reset_out;
  wire [3:0] A_q, adder_1_out, and_1_out, B_q, C_q, multiplier_1_cout, multiplier_1_out, not_1_out,
       not_2_out, or_1_out, shifter_1_out, shifter_2_out, shifter_3_out, shifter_4_out, xor_1_out;

  Button Reset (.out(Reset_out));
  Register #(.width(4)) A (.D(Datos), .Q(A_q), .clk(Set_A), .clr(Reset_out));  // open: en
  Register #(.width(4)) B (.D(Datos), .Q(B_q), .clk(Set_B), .clr(Reset_out));  // open: en
  Register #(.width(4)) C (.D(Datos), .Q(C_q), .clk(Set_C), .clr(Reset_out));  // open: en
  Pull_Resistor pull_resistor_1 (.node(Banderas));
  Pull_Resistor pull_resistor_2 (.node(A_q));
  Pull_Resistor pull_resistor_3 (.node(B_q));
  assign not_1_out = ~A_q;  // NOT_Gate not_1, 4 bits wide
  assign not_2_out = ~B_q;  // NOT_Gate not_2, 4 bits wide
  assign or_1_out = A_q | B_q;  // OR_Gate or_1, 4 bits wide
  assign and_1_out = A_q & B_q;  // AND_Gate and_1, 4 bits wide
  assign xor_1_out = A_q ^ B_q;  // XOR_Gate xor_1, 4 bits wide
  Adder #(.width(4)) adder_1 (.a(A_q), .b(B_q), .out(adder_1_out), .cout(Sobrecarga));  // open: cin
  Multiplier #(.width(4)) multiplier_1 (
    .a(A_q), .b(B_q), .out(multiplier_1_out), .cout(multiplier_1_cout));  // open: cin
  Shifter #(.width(4)) shifter_1 (.in(A_q), .\dist (B_q[1:0]), .out(shifter_1_out));
  Shifter #(.width(4), .shift("lr")) shifter_2 (.in(A_q), .\dist (B_q[1:0]), .out(shifter_2_out));
  Shifter #(.width(4), .shift("rl")) shifter_3 (.in(A_q), .\dist (B_q[1:0]), .out(shifter_3_out));
  Shifter #(.width(4), .shift("rr")) shifter_4 (.in(A_q), .\dist (B_q[1:0]), .out(shifter_4_out));
  Comparator #(.width(4)) comparator_1 (
    .a(B_q), .b(A_q), .gt(comparator_1_gt), .eq(comparator_1_eq), .lt(comparator_1_lt));
  or or_2 (or_2_out, comparator_1_gt, comparator_1_eq);
  or or_3 (or_3_out, comparator_1_eq, comparator_1_lt);
  Multiplexer #(.select(4), .width(4), .enable("false")) multiplexer_1 (
    .in0(A_q), .in1(B_q), .in2(not_1_out), .in3(not_2_out), .in4(or_1_out), .in5(and_1_out), .in6(xor_1_out),
    .in7(adder_1_out), .in8(multiplier_1_out), .in9(multiplier_1_cout), .in10(shifter_1_out),
    .in11(shifter_2_out), .in12(shifter_3_out), .in13(shifter_4_out), .in14(4'b0000), .in15(4'b1111),
    .out(Salida), .sel(C_q));
  not not_3 (not_3_out, comparator_1_eq);
  Multiplexer #(.select(3), .enable("false")) multiplexer_2 (
    .in0(comparator_1_gt), .in1(comparator_1_eq), .in2(comparator_1_lt), .in3(or_2_out), .in4(or_3_out),
    .in5(not_3_out), .in6(1'b0), .in7(1'b1), .out(Bandera), .sel(Banderas));
endmodule
