// Logisim project ALU.circ as structural Verilog
module ALU (
  input  [9:0] in_1,
  input  [3:0] RS,
  input  [3:0] RD,
  output [3:0] out_4,
  output OVERFLOW,
  output out_6
);

  wire a, and_1_out, and_2_out, and_3_out, and_4_out, b;
  wire [3:0] adder_1_out, adder_2_out, and_5_out, nor_1_out, or_1_out, subtractor_1_out, subtractor_2_out;

  and and_1 (and_1_out, ~in_1[7], ~in_1[6]);  // AND_Gate
  and and_2 (and_2_out, ~in_1[7], in_1[6]);  // AND_Gate
  and and_3 (and_3_out, in_1[7], ~in_1[6]);  // AND_Gate
  and and_4 (and_4_out, in_1[7], in_1[6]);
  assign b = and_1_out ? 1'b0 : 1'bz;  // Controlled_Buffer controlled_buffer_1
  assign b = and_2_out ? 1'b1 : 1'bz;  // Controlled_Buffer controlled_buffer_2
  assign b = and_3_out ? a : 1'bz;  // Controlled_Buffer controlled_buffer_3
  assign b = and_4_out ? ~a : 1'bz;  // Controlled_Inverter controlled_inverter_1
  assign or_1_out = RS | RD;  // OR_Gate or_1, 4 bits wide
  assign and_5_out = RS & RD;  // AND_Gate and_5, 4 bits wide
  Adder #(.width(4)) adder_1 (.a(RS), .b(RD), .out(adder_1_out));  // open: cin, cout
  Adder #(.width(4)) adder_2 (.a(RS), .b(RD), .out(adder_2_out), .cin(b), .cout(a));
  Subtractor #(.width(4)) subtractor_1 (.a(RS), .b(RD), .out(subtractor_1_out));  // open: bin, bout
  Subtractor #(.width(4)) subtractor_2 (.a(RS), .b(RD), .out(subtractor_2_out), .bin(b), .bout(a));
  assign nor_1_out = ~(RS | RD);  // NOR_Gate nor_1, 4 bits wide
  Subtractor #(.width(4)) subtractor_3 ();  // open: a, b, out, bin, bout
  Multiplexer #(.select(3), .width(4), .enable("false")) multiplexer_1 (
    .in0(adder_1_out), .in1(adder_2_out), .in2(subtractor_1_out), .in3(subtractor_2_out), .in4(or_1_out),
    .in5(and_5_out), .in6(nor_1_out), .out(out_4));  // open: in7, sel
  Comparator #(.width(4)) comparator_1 (.a(out_4), .b(4'b1111), .gt(OVERFLOW));  // open: eq, lt
  Comparator #(.width(4)) comparator_2 (.a(out_4), .b(4'b0000), .eq(out_6));  // open: gt, lt

  // Notes on the sheet:
  //   ADD
  //   ADC
  //   SUB
  //   SBB
  //   CERO
endmodule

module registros (
  input  [9:0] in_1
);

  wire _00_out, _01_out, _10_out, _11_out, and_1_out, clock_1_out;
  wire [3:0] controlled_buffer_1_out, controlled_buffer_2_out, controlled_buffer_4_out,
       controlled_buffer_6_out, controlled_buffer_8_out, controlled_buffer_9_out, R0_q, R1_q, R2_q, R3_q;

  and _00 (_00_out, ~in_1[0], ~in_1[1]);  // AND_Gate
  and _01 (_01_out, in_1[0], ~in_1[1]);  // AND_Gate
  and _10 (_10_out, ~in_1[0], in_1[1]);  // AND_Gate
  and _11 (_11_out, in_1[0], in_1[1]);
  Clock clock_1 (.out(clock_1_out));
  assign controlled_buffer_1_out = _00_out ? R0_q : 4'bz;  // Controlled_Buffer controlled_buffer_1
  Register #(.width(4)) R0 (.D(controlled_buffer_2_out), .en(_00_out), .Q(R0_q), .clk(clock_1_out));  // open: clr
  assign controlled_buffer_2_out = _00_out ? controlled_buffer_9_out : 4'bz;  // Controlled_Buffer controlled_buffer_2
  assign controlled_buffer_1_out = _01_out ? R1_q : 4'bz;  // Controlled_Buffer controlled_buffer_3
  Register #(.width(4)) R1 (.D(controlled_buffer_4_out), .en(_01_out), .Q(R1_q), .clk(clock_1_out));  // open: clr
  assign controlled_buffer_4_out = _01_out ? controlled_buffer_9_out : 4'bz;  // Controlled_Buffer controlled_buffer_4
  Register #(.width(4)) R2 (.D(controlled_buffer_6_out), .en(_10_out), .Q(R2_q), .clk(clock_1_out));  // open: clr
  assign controlled_buffer_1_out = _10_out ? R2_q : 4'bz;  // Controlled_Buffer controlled_buffer_5
  assign controlled_buffer_6_out = _10_out ? controlled_buffer_9_out : 4'bz;  // Controlled_Buffer controlled_buffer_6
  assign controlled_buffer_1_out = _11_out ? R3_q : 4'bz;  // Controlled_Buffer controlled_buffer_7
  Register #(.width(4)) R3 (.D(controlled_buffer_8_out), .en(_11_out), .Q(R3_q), .clk(clock_1_out));  // open: clr
  assign controlled_buffer_8_out = _11_out ? controlled_buffer_9_out : 4'bz;  // Controlled_Buffer controlled_buffer_8
  assign controlled_buffer_9_out = and_1_out ? {in_1[7:6], in_1[3:2]} : 4'bz;  // Controlled_Buffer controlled_buffer_9
  and and_1 (and_1_out, in_1[4], ~in_1[5], ~in_1[8], ~in_1[9]);  // AND_Gate

  // Notes on the sheet:
  //   INSTRUCCIONES DE E/S
endmodule
