// Logisim project p3-a.circ as structural Verilog: 1 circuit, main circuit main
module main (
  input  [7:0] in_1,
  input  [7:0] in_2,
  input  [3:0] in_3,
  input  ADC,
  input  SBB,
  input  INC,
  input  DEC,
  input  [2:0] in_8,
  input  [2:0] ROL,
  input  [2:0] in_10,
  input  [2:0] in_11,
  output SUB,
  output [7:0] out_13,
  output out_14
);

  wire [7:0] adder_1_out, adder_2_out, adder_3_out, and_1_out, not_1_out, or_1_out, shifter_1_out,
       shifter_2_out, shifter_3_out, shifter_4_out, subtractor_1_out, subtractor_2_out, subtractor_3_out,
       xor_1_out;

  assign and_1_out = in_1 & in_2;  // AND_Gate and_1, 8 bits wide
  assign or_1_out = in_1 | in_2;  // OR_Gate or_1, 8 bits wide
  assign xor_1_out = in_1 ^ in_2;  // XOR_Gate xor_1, 8 bits wide
  assign not_1_out = ~in_1;  // NOT_Gate not_1, 8 bits wide
  Adder adder_1 (.a(in_1), .b(in_2), .out(adder_1_out));  // open: cin, cout
  Adder adder_2 (.a(in_1), .b(in_2), .out(adder_2_out), .cin(ADC), .cout(SUB));
  Subtractor subtractor_1 (.a(in_1), .b(in_2), .out(subtractor_1_out));  // open: bin, bout
  Subtractor subtractor_2 (.a(in_1), .b(in_2), .out(subtractor_2_out), .bin(SBB), .bout(out_14));
  Adder adder_3 (.a(in_1), .b({8{1'b0}}), .out(adder_3_out), .cin(INC));  // open: cout
  Subtractor subtractor_3 (.a(in_1), .b({8{1'b0}}), .out(subtractor_3_out), .bin(DEC));  // open: bout
  Shifter shifter_1 (.in(in_1), .\dist (in_8), .out(shifter_1_out));
  Shifter #(.shift("lr")) shifter_2 (.in(in_1), .\dist (ROL), .out(shifter_2_out));
  Shifter #(.shift("rl")) shifter_3 (.in(in_1), .\dist (in_10), .out(shifter_3_out));
  Shifter #(.shift("rr")) shifter_4 (.in(in_1), .\dist (in_11), .out(shifter_4_out));
  Multiplexer #(.select(4), .width(8), .disabled(0), .enable("false")) multiplexer_1 (
    .in1(and_1_out), .in2(or_1_out), .in3(xor_1_out), .in4(not_1_out), .in5(adder_1_out), .in6(adder_2_out),
    .in7(subtractor_1_out), .in8(subtractor_2_out), .in9(adder_3_out), .in10(subtractor_3_out),
    .in11(shifter_1_out), .in12(shifter_2_out), .in13(shifter_3_out), .in14(shifter_4_out), .out(out_13),
    .sel(in_3));  // open: in0, in15

  // Notes on the sheet:
  //   ADD
  //   SHL
  //   SHR
  //   ROR
endmodule
