// Logisim project p4-2.circ as structural Verilog: 3 circuits, main circuit main
module main (
  input  [3:0] in_1,
  output [3:0] DIRECCION,
  output [7:0] INTRUCCION,
  output [3:0] out_4,
  output [7:0] out_5,
  output ACARREO,
  output CERO,
  output [3:0] out_8,
  output [7:0] CONTROL
);

  wire button_1_out, clock_1_out, controlled_buffer_2_out, decoder_1_out0, decoder_1_out1, decoder_1_out2,
       decoder_1_out3, not_1_out, not_2_out, not_3_out, not_4_out, not_5_out;
  wire [1:0] multiplexer_1_out;
  wire [3:0] controlled_buffer_1_out, controlled_buffer_4_out, controlled_buffer_5_out,
       controlled_buffer_6_out, controlled_buffer_7_out, controlled_buffer_9_out, controlled_buffer_12_out,
       controlled_buffer_14_out, counter_1_q, register_1_q, register_2_q, register_3_q, register_4_q,
       register_5_q, register_6_q;
  wire [7:0] counter_2_q;

  Counter #(.width(4), .max('hf)) counter_1 (
    .load(CONTROL[1]), .D(DIRECCION), .count(not_1_out), .Q(counter_1_q), .clk(CONTROL[7]));  // open: carry, clr
  not not_1 (not_1_out, CONTROL[1]);
  not not_2 (not_2_out, CONTROL[6]);
  Clock clock_1 (.out(clock_1_out));
  ROM #(.addrWidth(4)) rom_1 (.addr(counter_1_q), .data({INTRUCCION[7:4], DIRECCION}));  // open: sel
  DECODIFICADOR decodificador_1 (.OP_CC(INTRUCCION[7:4]), .DIRECCION(out_5));
  Counter counter_2 (
    .load(CONTROL[6]), .D(out_5), .count(not_2_out), .Q(counter_2_q), .clk(clock_1_out));  // open: carry, clr
  Multiplexer #(.width(2), .enable("false")) multiplexer_1 (
    .in0(DIRECCION[1:0]), .in1(DIRECCION[3:2]), .out(multiplexer_1_out), .sel(CONTROL[5]));
  Button button_1 (.out(button_1_out));
  ROM rom_2 (.addr(counter_2_q), .data(CONTROL));  // open: sel
  Decoder #(.select(2), .enable("false")) decoder_1 (
    .out0(decoder_1_out0), .out1(decoder_1_out1), .out2(decoder_1_out2), .out3(decoder_1_out3),
    .sel(multiplexer_1_out));
  assign controlled_buffer_1_out = decoder_1_out0 ? controlled_buffer_12_out : 4'bz;  // Controlled_Buffer controlled_buffer_1
  assign controlled_buffer_2_out = CONTROL[2] ? button_1_out : 1'bz;  // Controlled_Buffer controlled_buffer_2
  assign controlled_buffer_2_out = not_3_out ? CONTROL[0] : 1'bz;  // Controlled_Buffer controlled_buffer_3
  not not_3 (not_3_out, CONTROL[2]);
  not not_4 (not_4_out, CONTROL[5]);
  Register #(.width(4)) register_1 (
    .D(controlled_buffer_1_out), .en(decoder_1_out0), .Q(register_1_q), .clk(controlled_buffer_2_out));  // open: clr
  assign controlled_buffer_4_out = decoder_1_out1 ? controlled_buffer_12_out : 4'bz;  // Controlled_Buffer controlled_buffer_4
  assign controlled_buffer_5_out = decoder_1_out0 ? register_1_q : 4'bz;  // Controlled_Buffer controlled_buffer_5
  assign controlled_buffer_6_out = CONTROL[4] ? controlled_buffer_5_out : 4'bz;  // Controlled_Buffer controlled_buffer_6
  Register #(.width(4)) register_2 (
    .D(controlled_buffer_4_out), .en(decoder_1_out1), .Q(register_2_q), .clk(controlled_buffer_2_out));  // open: clr
  assign controlled_buffer_7_out = decoder_1_out2 ? controlled_buffer_12_out : 4'bz;  // Controlled_Buffer controlled_buffer_7
  assign controlled_buffer_5_out = decoder_1_out1 ? register_2_q : 4'bz;  // Controlled_Buffer controlled_buffer_8
  Register #(.width(4)) register_3 (
    .D(controlled_buffer_6_out), .en(not_4_out), .Q(register_3_q), .clk(CONTROL[0]));  // open: clr
  Register #(.width(4)) register_4 (
    .D(controlled_buffer_6_out), .en(CONTROL[5]), .Q(register_4_q), .clk(CONTROL[0]));  // open: clr
  Register #(.width(4)) register_5 (
    .D(controlled_buffer_7_out), .en(decoder_1_out2), .Q(register_5_q), .clk(controlled_buffer_2_out));  // open: clr
  assign controlled_buffer_9_out = decoder_1_out3 ? controlled_buffer_12_out : 4'bz;  // Controlled_Buffer controlled_buffer_9
  assign controlled_buffer_5_out = decoder_1_out2 ? register_5_q : 4'bz;  // Controlled_Buffer controlled_buffer_10
  ALU alu_1 (.A(register_3_q), .B(register_4_q), .ACARREO(ACARREO), .F(INTRUCCION[7:4]), .ZERO(CERO), .R(out_8));
  Register #(.width(4)) register_6 (
    .D(controlled_buffer_9_out), .en(decoder_1_out3), .Q(register_6_q), .clk(controlled_buffer_2_out));  // open: clr
  assign controlled_buffer_5_out = decoder_1_out3 ? register_6_q : 4'bz;  // Controlled_Buffer controlled_buffer_11
  assign controlled_buffer_12_out = not_5_out ? out_8 : 4'bz;  // Controlled_Buffer controlled_buffer_12
  not not_5 (not_5_out, CONTROL[4]);
  assign controlled_buffer_12_out = CONTROL[2] ? in_1 : 4'bz;  // Controlled_Buffer controlled_buffer_13
  Hex_Digit_Display hex_digit_display_1 (.value(controlled_buffer_14_out));  // open: dp
  assign controlled_buffer_14_out = CONTROL[3] ? controlled_buffer_5_out : 4'bz;  // Controlled_Buffer controlled_buffer_14

  assign INTRUCCION[3:0] = DIRECCION;
  assign out_4 = INTRUCCION[7:4];

  // Other names for the same wires on the sheet: CLK = CONTROL[0]; LOAD = CONTROL[1]; IN = CONTROL[2];
  //   OUT = CONTROL[3]; W_R = CONTROL[4]; S_D = CONTROL[5]; CP = CONTROL[6]; CLOK = CONTROL[7];
  //   FUNCION[3:0] = INTRUCCION[7:4]

  // Notes on the sheet:
  //   PC
  //   PROGRAMA
  //   DECODIFICADOR
  //   OP CC RD RS
  //   contents of rom_1 (hex, n*v repeats v):
  //   c0 c1 e1 d5 0 10 45 c 64 bc a2 95
  //   MAQUINAS DE ESTADO
  //   contents of rom_2 (hex, n*v repeats v):
  //   40 15*0 10 11 30 21 20 23 10 d0 8*0 14 d0 14*0 18 d0 14*0 12 92 d0
  //   0
  //   1
  //   A
  //   B
  //   REGISTROS
  //   2
  //   ALU
  //   3
endmodule

module DECODIFICADOR (
  input  [3:0] OP_CC,
  output [7:0] DIRECCION
);

  wire and_1_out, comparator_1_eq, comparator_1_gt, comparator_1_lt, comparator_2_eq, comparator_2_lt;

  Comparator #(.width(4), .mode("unsigned")) comparator_1 (
    .a(OP_CC), .b(4'b1100), .gt(comparator_1_gt), .eq(comparator_1_eq), .lt(comparator_1_lt));
  assign DIRECCION = comparator_1_lt ? 8'h10 : 8'bz;  // Controlled_Buffer controlled_buffer_1
  Comparator #(.width(4), .mode("unsigned")) comparator_2 (
    .a(OP_CC), .b(4'b1110), .eq(comparator_2_eq), .lt(comparator_2_lt));  // open: gt
  assign DIRECCION = comparator_2_eq ? 8'h30 : 8'bz;  // Controlled_Buffer controlled_buffer_2
  and and_1 (and_1_out, comparator_1_gt, comparator_2_lt);
  assign DIRECCION = and_1_out ? 8'h40 : 8'bz;  // Controlled_Buffer controlled_buffer_3
  assign DIRECCION = comparator_1_eq ? 8'h20 : 8'bz;  // Controlled_Buffer controlled_buffer_4

  // Notes on the sheet:
  //   1100
  //   1110
  //   DECODIFICADOR DE INTRUCCION
  //   OPERACION
  //   SALIDA
  //   SALTO
  //   ENTRADA
endmodule

module ALU (
  input  [3:0] A,
  input  [3:0] B,
  input  [3:0] F,
  output ZERO,
  output [3:0] R,
  output ACARREO
);

  wire adder_1_cout, adder_2_cout, adder_3_cout, not_1_out, subtractor_1_bout, subtractor_2_bout,
       subtractor_3_bout;
  wire [3:0] adder_1_out, adder_2_out, adder_3_out, not_2_out, shifter_1_out, shifter_2_out, shifter_3_out,
       shifter_4_out, subtractor_1_out, subtractor_2_out, subtractor_3_out, xor_1_out, xor_2_out;

  not not_1 (not_1_out, 1'b0);
  assign not_2_out = ~A;  // NOT_Gate not_2, 4 bits wide
  Subtractor #(.width(4)) subtractor_1 (
    .a(A), .b(4'b0001), .out(subtractor_1_out), .bout(subtractor_1_bout));  // open: bin
  Adder #(.width(4)) adder_1 (.a(A), .b(B), .out(adder_1_out), .cin(1'b0), .cout(adder_1_cout));
  Adder #(.width(4)) adder_2 (.a(B), .b(A), .out(adder_2_out), .cout(adder_2_cout));  // open: cin
  Subtractor #(.width(4)) subtractor_2 (
    .a(B), .b(A), .out(subtractor_2_out), .bin(not_1_out), .bout(subtractor_2_bout));
  assign xor_1_out = A ^ A;  // XOR_Gate xor_1, 4 bits wide
  Subtractor #(.width(4)) subtractor_3 (
    .a(A), .b(4'b0001), .out(subtractor_3_out), .bout(subtractor_3_bout));  // open: bin
  Shifter #(.width(4)) shifter_1 (.in(A), .\dist (2'b11), .out(shifter_1_out));
  Shifter #(.width(4), .shift("lr")) shifter_2 (.in(A), .\dist (2'b11), .out(shifter_2_out));
  Shifter #(.width(4), .shift("rl")) shifter_3 (.in(A), .\dist (2'b11), .out(shifter_3_out));
  Shifter #(.width(4), .shift("rr")) shifter_4 (.in(A), .\dist (2'b11), .out(shifter_4_out));
  Adder #(.width(4)) adder_3 (.a(A), .b(4'b0001), .out(adder_3_out), .cout(adder_3_cout));  // open: cin
  assign xor_2_out = A ^ B;  // XOR_Gate xor_2, 4 bits wide
  Multiplexer #(.select(4), .width(4), .disabled(0), .enable("false")) multiplexer_1 (
    .in0(A), .in1(adder_3_out), .in2(xor_2_out), .in3(not_2_out), .in4(subtractor_1_out), .in5(adder_1_out),
    .in6(adder_2_out), .in7(shifter_2_out), .in8(subtractor_3_out), .in9(xor_1_out), .in10(shifter_1_out),
    .in11(subtractor_2_out), .in12(shifter_3_out), .in13(shifter_4_out), .out(R), .sel(F));  // open: in14, in15
  Multiplexer #(.select(4), .disabled(0), .enable("false")) multiplexer_2 (
    .in1(adder_3_cout), .in4(subtractor_1_bout), .in5(adder_1_cout), .in6(adder_2_cout),
    .in9(subtractor_3_bout), .in11(subtractor_2_bout), .out(ACARREO), .sel(F));  // open: in0, in2, in3, in7, in8, in10, in12, in13, in14, in15
  Comparator #(.width(4)) comparator_1 (.a(4'b0000), .b(R), .eq(ZERO));  // open: gt, lt

  // Notes on the sheet:
  //   FUNCION
  //   MOVE = 0
  //   INCREMENTO =1
  //   DECREMENTO =4
  //   SUMA = 6
  //   CLEAR = 9
  //   SHIFT = 10
  //   RESTA =11
endmodule
